// Logisim project CC4N-CPU.circ as structural Verilog: 3 circuits, main circuit main
module main (
  input  in_1,
  input  in_2,
  input  in_3,
  output out_4,
  output out_5
);

  ADD_1 add_1_1 (.Vai_1(out_4), .A(in_1), .B(in_2), .C(in_3), .S(out_5));
endmodule

module ADD_1 (
  input  A,
  input  B,
  input  C,
  output S,
  output Vai_1
);

  wire and_1_out, and_2_out, or_1_out, xor_1_out;

  xor xor_1 (xor_1_out, B, C);
  or or_1 (or_1_out, B, C);
  and and_1 (and_1_out, B, C);
  xor xor_2 (S, xor_1_out, A);
  and and_2 (and_2_out, or_1_out, A);
  or or_2 (Vai_1, and_2_out, and_1_out);
endmodule

module ADD_4 (
  input  [3:0] in_1,
  input  [3:0] in_2,
  output out_3,
  output [3:0] out_4
);

  wire add_1_2_vai_1, add_1_3_vai_1, add_1_4_vai_1;

  // Probe on in_2
  ADD_1 add_1_1 (.Vai_1(out_3), .A(in_2[3]), .B(in_1[3]), .C(add_1_2_vai_1), .S(out_4[3]));
  ADD_1 add_1_2 (.Vai_1(add_1_2_vai_1), .A(in_2[2]), .B(in_1[2]), .C(add_1_3_vai_1), .S(out_4[2]));
  // Probe on out_4
  // Probe on in_1
  ADD_1 add_1_3 (.Vai_1(add_1_3_vai_1), .A(in_2[1]), .B(in_1[1]), .C(add_1_4_vai_1), .S(out_4[1]));
  ADD_1 add_1_4 (.Vai_1(add_1_4_vai_1), .A(in_2[0]), .B(in_1[0]), .C(1'b0), .S(out_4[0]));
endmodule
